# Fritzing sketch fritzing (saved by Fritzing 0.7.7b)
breadboards: 1

parts:
  Arduino_Uno = Arduino
  button1 = Square Pushbutton
  button3 = Square Pushbutton
  button2 = Square Pushbutton
  button1_resistor = Resistor [tolerance=±5% resistance=10k package=THT]
  button2_resistor = Resistor [tolerance=±5% resistance=10k package=THT]
  button3_resistor = Resistor [tolerance=±5% resistance=10k package=THT]
  Electret_Microphone = Breakout Board for Electret Microphone
  LED1 = LED - 5mm [color="Green (555nm)" package="5 mm [THT]"]

nets:
  N1: Arduino_Uno.aref, Arduino_Uno.3V3, Electret_Microphone.AUD
  GND: Arduino_Uno.GND, button1_resistor.Pin_1, button2_resistor.Pin_1, button3_resistor.Pin_1, Electret_Microphone.GND, LED1.cathode
  N2: Arduino_Uno.D12, LED1.anode
  N3: Arduino_Uno.D8, button3.leg1, button3_resistor.Pin_0
  N4: Arduino_Uno.D7, button2.leg1, button2_resistor.Pin_0
  N5: Arduino_Uno.D4, button1.leg1, button1_resistor.Pin_0
  N6: Arduino_Uno.+5V, button1.leg0, button3.leg0, button2.leg0
  N7: Arduino_Uno.A1, Electret_Microphone.VCC
